// Logisim project CPU.circ as structural Verilog: 6 circuits, main circuit main
module main (
  input  [17:0] in_1,
  input  in_2,
  input  in_3,
  input  [3:0] in_4,
  output [17:0] out_5
);

  wire and_1_out, and_2_out, and_3_out, B0, B1, B2, B3, B4, B5, B6, B7, B8, B9, B10, B11, clock_1_out, D15,
       I0, I1, I2, I3, not_1_out, not_2_out, T3;
  wire [14:0] instruction_decoder_1_opt_code;

  Clock clock_1 (.out(clock_1_out));
  not not_1 (not_1_out, in_3);
  Timer timer_1 (
    .Clock(clock_1_out), .T3(T3));  // open: Increment, Clear, T0, T1, T2, T4, T5, T6, T7, T8, T9, T10, T11, T12, T13, T14, T15, Overflow
  Bus bus_1 (.Input_Bits(in_1), .Reset(not_1_out), .Set(in_3), .Clock(clock_1_out), .Selection_Bit(in_4), .OUT(out_5));
  Instruction_Decoder instruction_decoder_1 (
    ._18_Bit_Input(in_1), .Enable(in_2), .Addressing_Mode({I3, I2, I1, I0}),
    .Opt_Code({D15, instruction_decoder_1_opt_code}),
    .Data({B11, B10, B9, B8, B7, B6, B5, B4, B3, B2, B1, B0}));
  and and_1 (and_1_out, I0, D15, T3);
  not not_2 (not_2_out, and_2_out);
  and and_2 (and_2_out, B0, B1, B2, B3, B4, B5, B6, B7, B8, B9, B10, B11);
  and and_3 (and_3_out, and_1_out, not_2_out);
  Register #(.width(12)) Accumulator (.clr(and_3_out));  // open: D, en, Q, clk
endmodule

module Timer (
  input  Increment,
  input  Clock,
  input  Clear,
  output T0,
  output T1,
  output T2,
  output T3,
  output T4,
  output T5,
  output T6,
  output T7,
  output T8,
  output T9,
  output T10,
  output T11,
  output T12,
  output T13,
  output T14,
  output T15,
  output Overflow
);

  wire [3:0] counter_1_q;

  Counter #(.width(4), .max('hf)) counter_1 (
    .count(Increment), .Q(counter_1_q), .carry(Overflow), .clk(Clock), .clr(Clear));  // open: load, D
  Decoder #(.select(4)) decoder_1 (
    .out0(T0), .out1(T1), .out2(T2), .out3(T3), .out4(T4), .out5(T5), .out6(T6), .out7(T7), .out8(T8),
    .out9(T9), .out10(T10), .out11(T11), .out12(T12), .out13(T13), .out14(T14), .out15(T15), .sel(counter_1_q));  // open: en
endmodule

module Bus (
  input  [17:0] Input_Bits,
  input  Reset,
  input  Set,
  input  Clock,
  input  [3:0] Selection_Bit,
  output [17:0] OUT
);

  wire AC, and_1_out, and_2_out, AR, DR, INPR, IR, IX, OUTR, PC, TR;
  wire [11:0] IX_q, n18b212b_1__12b_output;
  wire [17:0] _12B218B__18b_output;

  and and_1 (and_1_out, IX, Set);
  _18B212B u_18b212b_1 (._12b_Output(n18b212b_1__12b_output), ._18b_input(Input_Bits));
  Decoder #(.select(4)) decoder_1 (
    .out0(IX), .out1(AR), .out2(PC), .out3(DR), .out4(AC), .out5(IR), .out6(TR), .out7(INPR), .out8(OUTR),
    .sel(Selection_Bit), .en(Clock));  // open: out9, out10, out11, out12, out13, out14, out15
  Register #(.width(12)) u_IX (.D(n18b212b_1__12b_output), .en(and_1_out), .Q(IX_q), .clk(Clock), .clr(and_2_out));
  _12_2_18_bus _12B218B (._12b_Input(IX_q), ._18b_output(_12B218B__18b_output));
  and and_2 (and_2_out, IX, Reset);
  Multiplexer #(.select(4), .width(18)) multiplexer_1 (
    .in0(_12B218B__18b_output), .out(OUT), .sel(Selection_Bit), .en(Clock));  // open: in1, in2, in3, in4, in5, in6, in7, in8, in9, in10, in11, in12, in13, in14, in15

  // Other names for the same wires on the sheet: DATA[17:0] = Input_Bits; rset = Reset
endmodule

// ID
module Instruction_Decoder (
  input  [17:0] _18_Bit_Input,
  input  Enable,
  output [3:0] Addressing_Mode,
  output [15:0] Opt_Code,
  output [11:0] Data
);

  Decoder #(.select(2)) decoder_1 (
    .out0(Addressing_Mode[0]), .out1(Addressing_Mode[1]), .out2(Addressing_Mode[2]),
    .out3(Addressing_Mode[3]), .sel(_18_Bit_Input[17:16]), .en(Enable));
  Decoder #(.select(4)) decoder_2 (
    .out0(Opt_Code[0]), .out1(Opt_Code[1]), .out2(Opt_Code[2]), .out3(Opt_Code[3]), .out4(Opt_Code[4]),
    .out5(Opt_Code[5]), .out6(Opt_Code[6]), .out7(Opt_Code[7]), .out8(Opt_Code[8]), .out9(Opt_Code[9]),
    .out10(Opt_Code[10]), .out11(Opt_Code[11]), .out12(Opt_Code[12]), .out13(Opt_Code[13]),
    .out14(Opt_Code[14]), .out15(Opt_Code[15]), .sel(_18_Bit_Input[15:12]), .en(Enable));

  assign Data = _18_Bit_Input[11:0];

  // Other names for the same wires on the sheet: ENB = Enable
endmodule

module _12_2_18_bus (
  input  [11:0] _12b_Input,
  output [17:0] _18b_output
);


  assign _18b_output = {_12b_Input[0], _12b_Input[1], _12b_Input[2], _12b_Input[3], _12b_Input[4], _12b_Input[5], _12b_Input[6], _12b_Input[7], _12b_Input[8], _12b_Input[9], _12b_Input[10], _12b_Input[11], {6{1'b0}}};

  // Notes on the sheet:
  //   TODO: Manage orientation of these lines
endmodule

module _18B212B (
  input  [17:0] _18b_input,
  output [11:0] _12b_Output
);


  assign _12b_Output = {_18b_input[6], _18b_input[7], _18b_input[8], _18b_input[9], _18b_input[10], _18b_input[11], _18b_input[12], _18b_input[13], _18b_input[14], _18b_input[15], _18b_input[16], _18b_input[17]};

  // Notes on the sheet:
  //   TODO: Manage orientation of these lines
endmodule
